# Fritzing sketch AutoTurntable (saved by Fritzing 0.9.9b)
circuit board: 18.1572cm x 16.2335cm
breadboards: 2

parts:
  A1 = Arduino Nano (Rev3.0)
  J7 = shrouded pin header, 6 pins [form="♂ (shrouded male)"]
  J1 = Screw terminal - 2 pins [package=THT]
  J14 = shrouded pin header, 6 pins [form="♂ (shrouded male)"]
  JP1 = male pin header, 3 pins [form="♂ (male)"]
  J10 = shrouded pin header, 6 pins [form="♂ (shrouded male)"]
  C1 = Electrolytic Capacitor [capacitance=3.3µF voltage=50V package="100 mil [THT, electrolytic]"]
  R4 = Resistor [tolerance=±5% power=0.25 resistance=1k package=THT]
  J13 = shrouded pin header, 8 pins [form="♂ (shrouded male)"]
  R5 = Resistor [tolerance=±5% power=0.25 resistance=1k package=THT]
  R6 = Resistor [tolerance=±5% power=0.25 resistance=1k package=THT]
  R7 = Resistor [tolerance=±5% power=0.25 resistance=1k package=THT]
  D1 = Rectifier Diode [part_number=1N007 package="300 mil [THT]"]
  U2 = ADG333AB [chip_label=U package="DIP (Dual Inline) [THT]"]
  R8 = Resistor [tolerance=±5% power=0.25 resistance=1k package=THT]
  Q2 = Basic FET P-Channel [part_number=TIP120 package="TO220 [THT]"]
  U3 = ULN2003A [package="DIP16 [THT]"]
  U4 = ULN2003A [package="DIP16 [THT]"]
  C2 = Tantalum Capacitor [capacitance=20nF voltage=35V package="C 6032 [SMD, tantalum]"]
  R9 = Resistor [tolerance=±5% power=0.25 resistance=10k package=THT]
  R10 = Resistor [tolerance=±5% power=0.25 resistance=10k package=THT]
  R11 = Resistor [tolerance=±5% power=0.25 resistance=10k package=THT]
  R12 = Resistor [tolerance=±5% power=0.25 resistance=10k package=THT]
  R13 = Resistor [tolerance=±5% power=0.25 resistance=10k package=THT]
  R14 = Resistor [tolerance=±5% power=0.25 resistance=10k package=THT]
  R15 = Resistor [tolerance=±5% power=0.25 resistance=10k package=THT]
  P2 = POT [package=pot_alpha_rv16af-20]
  P3 = POT [package=pot_alpha_rv16af-20]
  P4 = POT [package=pot_alpha_rv16af-20]
  P5 = POT [package=pot_alpha_rv16af-20]
  P1 = POT [package=pot_alpha_rv16af-20]
  R16 = Resistor [tolerance=±5% power=0.25 resistance=10k package=THT]
  R17 = Resistor [tolerance=±5% power=0.25 resistance=10k package=THT]
  R18 = Resistor [tolerance=±5% power=0.25 resistance=10k package=THT]
  R19 = Resistor [tolerance=±5% power=0.25 resistance=10k package=THT]
  R20 = Resistor [tolerance=±5% power=0.25 resistance=10k package=THT]
  R21 = Resistor [tolerance=±5% power=0.25 resistance=10k package=THT]
  R22 = Resistor [tolerance=±5% power=0.25 resistance=10k package=THT]
  Q3 = Basic FET P-Channel [part_number=TIP120 package="TO220 [THT]"]
  D2 = Rectifier Diode [part_number=1N007 package="300 mil [THT]"]
  R23 = Resistor [tolerance=±5% power=0.25 resistance=1k package=THT]
  IC1 = IC, DIP package, 28 pins [chip_label=IC]
  J20 = Header 2 [package=molex-1x2_lock]
  J18 = Header 2 [package=molex-1x2_lock]
  J19 = Header 2 [package=molex-1x2_lock]
  J21 = Header 2 [package=molex-1x2_lock]
  J17 = Header 2 [package=molex-1x2_lock]
  J28 = female pin header, 2 pins [form="♀ (female)"]
  R24 = Resistor [tolerance=±5% power=0.25 resistance=10k package=THT]
  J29 = male pin header, 4 pins [form="♂ (male)"]
  J12 = male pin header, 5 pins [form="♂ (male)"]
  J3 = male pin header, 3 pins [form="♂ (male)"]
  J4 = male pin header, 3 pins [form="♂ (male)"]
  J2 = male pin header, 3 pins [form="♂ (male)"]
  J5 = male pin header, 2 pins [form="♂ (male)"]
  J16 = male pin header, 5 pins [form="♂ (male)"]
  J15 = male pin header, 5 pins [form="♂ (male)"]
  J30 = male pin header, 3 pins [form="♂ (male)"]
  J31 = male pin header, 3 pins [form="♂ (male)"]
  J22 = male pin header, 3 pins [form="♂ (male)"]
  J23 = male pin header, 3 pins [form="♂ (male)"]
  J24 = male pin header, 3 pins [form="♂ (male)"]
  J25 = male pin header, 3 pins [form="♂ (male)"]
  J26 = male pin header, 3 pins [form="♂ (male)"]
  J27 = male pin header, 3 pins [form="♂ (male)"]
  J34 = shrouded pin header, 16 pins [form="♂ (shrouded male)"]
  U5 = TC7SU04F [package=sot23-5]
  D3 = Rectifier Diode [part_number=1N007 package="300 mil [THT]"]
  D4 = Rectifier Diode [part_number=1N007 package="300 mil [THT]"]
  D5 = Rectifier Diode [part_number=1N007 package="300 mil [THT]"]
  D6 = Rectifier Diode [part_number=1N007 package="300 mil [THT]"]

nets:
  N1: A1.D1/TX, J28.pin2
  N2: A1.D0/RX, J28.pin1
  GND: A1.GND, J1.pin2, C1.-, R4.Pin_1, R5.Pin_1, R6.Pin_1, R7.Pin_1, U2.VSS, U2.GND, Q2.source, U3.0V, U4.0V, C2.+, R9.Pin_1, R10.Pin_1, R11.Pin_1, R12.Pin_1, R13.Pin_0, R14.Pin_0, R15.Pin_0, R16.Pin_0, R17.Pin_0, R18.Pin_0, R19.Pin_0, R20.Pin_0, R21.Pin_0, R22.Pin_0, Q3.source, IC1.pin12, IC1.pin27, R24.Pin_1, J29.pin2, J3.pin1, J3.pin2, J3.pin3, J22.pin3, J23.pin3, J24.pin3, J25.pin3, J26.pin3, J27.pin3, J34.pin16, U5.GND
  N3: A1.D2, IC1.pin17
  N4: A1.D3, IC1.pin16
  N5: A1.D4, IC1.pin15
  N6: A1.D5, IC1.pin14
  N7: A1.D6, IC1.pin28
  N8: A1.D7, U2.D1
  N9: A1.D8, U2.D2
  N10: A1.D9, U2.D3
  N11: A1.D10, U2.D4
  N12: A1.D11/MOSI, U2.IN1, U2.IN2, U2.IN3, U2.IN4
  N13: A1.D12/MISO, J13.pin4, J34.pin5
  VIN: A1.VIN, J7.pin1, J7.pin3, J14.pin2, J14.pin5, JP1.pin2, J10.pin2, C1.+, J13.pin1, D1.cathode, U2.VDD, U3.COM_-_Common, U4.COM_-_Common, C2.-, IC1.pin18, J18.1, J19.1, J17.1, J29.pin1, J2.pin1, J2.pin2, J2.pin3, J16.pin1, J15.pin1, J30.pin2, J31.pin2, J22.pin2, J23.pin2, J24.pin2, J25.pin2, J26.pin2, J27.pin2, J34.pin1, U5.+V, D5.anode, D6.anode
  N14: A1.A7, R8.Pin_0
  N15: A1.A6, P5.A
  N16: A1.A5, J29.pin4
  N17: A1.A4, J29.pin3
  N18: A1.A3, P4.A
  N19: A1.A2, P3.A
  N20: A1.A1, P2.A
  N21: A1.A0, P1.A
  N22: A1.3V3, J4.pin1, J4.pin2, J4.pin3
  N23: A1.D13/SCK, J13.pin3, J34.pin6
  N24: J7.pin2, J7.pin5, J1.pin1
  N25: J7.pin6, R15.Pin_1, IC1.pin8, J34.pin14
  N26: J14.pin4, JP1.pin3, R14.Pin_1, IC1.pin10
  N27: J14.pin6, JP1.pin1, R13.Pin_1, IC1.pin11
  N28: J10.pin1, J10.pin3, J13.pin2, J34.pin7
  N29: J10.pin4, J30.pin1, J34.pin9
  N30: J10.pin5, D2.cathode, J12.pin2, J34.pin10
  N31: J10.pin6, J31.pin1, J34.pin8
  N32: R4.Pin_0, J13.pin5
  N33: J13.pin6, R5.Pin_0
  N34: J13.pin7, R6.Pin_0
  N35: J13.pin8, R7.Pin_0
  N36: D1.anode, Q2.drain, J17.2
  N37: U2.S1A, U4.In_1
  N38: U2.S1B, U3.In_1
  N39: U2.S2B, U3.In_2
  N40: U2.S2A, U4.In_2
  N41: U2.S3A, U4.In_3
  N42: U2.S3B, U3.In_3
  N43: U2.S4B, U3.In_4
  N44: U2.S4A, U4.In_4
  N45: R8.Pin_1, Q2.gate
  N46: U3.Out_4, J15.pin5
  N47: U3.Out_3, J15.pin4
  N48: U3.Out_2, J15.pin3
  N49: U3.Out_1, J15.pin2
  N50: U4.Out_4, J16.pin5
  N51: U4.Out_3, J16.pin4
  N52: U4.Out_2, J16.pin3
  N53: U4.Out_1, J16.pin2
  N54: R9.Pin_0, IC1.pin19, J18.2
  N55: R10.Pin_0, IC1.pin20, J19.2
  N56: R11.Pin_0, IC1.pin21, J20.2, D4.cathode
  N57: R12.Pin_0, IC1.pin22, J21.2, D3.cathode
  N58: P2.S, P3.S, P4.S, P5.S, P1.S, IC1.pin1
  N59: P2.E, R19.Pin_1
  N60: P3.E, R18.Pin_1
  N61: P4.E, R17.Pin_1
  N62: P5.E, R16.Pin_1
  N63: P1.E, R20.Pin_1
  N64: R21.Pin_1, J31.pin3
  N65: R22.Pin_1, J30.pin3
  N66: Q3.gate, R23.Pin_1
  N67: Q3.drain, D2.anode, J12.pin1
  N68: R23.Pin_0, U5.OUT
  N69: IC1.pin4, J5.pin1
  N70: IC1.pin5, J5.pin2
  N71: IC1.pin6, R24.Pin_0, J34.pin15
  N72: IC1.pin7, J27.pin1
  N73: IC1.pin9, J26.pin1
  N74: IC1.pin23, J22.pin1
  N75: IC1.pin24, J23.pin1
  N76: IC1.pin25, J24.pin1
  N77: IC1.pin26, J25.pin1, J34.pin2, U5.IN
  N78: J20.1, D5.cathode
  N79: J21.1, D6.cathode
  N80: J12.pin3, J12.pin4
  N81: J34.pin3, D3.anode
  N82: J34.pin4, D4.anode

notes:
  Power SW
  DC in
  Speed SW
  Size SW
  Size Jumper
  12" Play Sensor
  LEDs
  PW SW
  SZ SW
  7-Seg Disp.
  Solenoid
  7S DISP
  SOl
  7"
  12"
  NC = 10"
  Vertical Motor
  Horiz. Motor
  [
  Upper Limit
  Lower Limit
  V MTR
  H MTR
  Pause Button
  Play/Home Button
  U LIM
  L LIM
  PAUS BTN
  PLY BTN
  7" Play Sensor
  10" Play Sensor
  Home Sensor
  7" SEN
  10" SEN
  12" SEN
  HOME SEN
  Pickup Sensor
  Speed Sensor
  Unused Mux Pins
  5v DC
  3.3v DC
  GND
  SPD SEN
  PKU SEN
  Mux In
  S15
  S16
  7" Cal Pot
  10" Cal Pot
  12" Cal Pot
  Home Cal Pot
  Pickup Del Pot
  5v DC In
  +
  -
  33-RPM Pot
  45-RPM Pot
  33-RPM POT
  45-RPM POT
  TURN MTR
  SPD SW
  7" CAL
  10" CAL
  12" CAL
  HOME CAL
  PKU DEL
  Automatic Changer Comm
  D1
  D0
  Arduino I/O
  _
  +5v
  Mux S16
  Mux S15
  Auto-mode indicator (Mux S12)
  5v DC in
  5v DC out
  NC
  Turntable power indicator LED
  33-RPM pot
  J12 pin 2
  45-RPM pot
  J12 pin 3
  J12 pin 4
  Q3 drain
  J10 pin 5
  Power indicator LED (5v)
  Turntable power indicator LED (J10 pin 3)
  Pause status LED (Ard. D13)
  Play status LED (Ard. D12)
  Play status LED GND
  Pause status LED GND
  Turntable power indicator LED GND
  Power indicator LED GND
  SW 1
  SW 2
  SW 3
  SW 4
  SW 5
  SW 6
  5v
  DATA
  PWR
  TRN PWR
  PAUSE
  MOVE
  SDA
  SCL
  ADJUST
  PULL
  HOME ST
  CLR ERR
  AUT ST
  PAUSE CMD
  PLAY CMD
  PLAY STATUS
  PAUSE STATUS
  TURN SPIN ST
  33 POT

custom parts:
  ADG333AB: A DIP stand-in part for whatever IC you want. With 20 pins on a 300mil dual inline package (DIP) footprint.
