# Fritzing sketch TurntableMain (saved by Fritzing 0.9.9b)
circuit board: 8cm x 8cm
breadboards: 3

parts:
  A1 = Arduino Nano (Rev3.0)
  J3 = shrouded pin header, 6 pins [form="♂ (shrouded male)"]
  J4 = shrouded pin header, 6 pins [form="♂ (shrouded male)"]
  J28 = shrouded pin header, 8 pins [form="♂ (shrouded male)"]
  U3 = ULN2003A [package="DIP16 [THT]"]
  U2 = ULN2003A [package="DIP16 [THT]"]
  J10 = male pin header, 5 pins [form="♂ (male)"]
  J11 = male pin header, 5 pins [form="♂ (male)"]
  J24 = male pin header, 3 pins [form="♂ (male)"]
  J25 = male pin header, 3 pins [form="♂ (male)"]
  J19 = shrouded pin header, 16 pins [form="♂ (shrouded male)"]
  J1 = screw terminal, 2 pins
  R24 = Resistor [tolerance=±5% resistance=10k power=0.25 package="0603 [SMD]"]
  R22 = Resistor [tolerance=±5% resistance=10k power=0.25 package="0603 [SMD]"]
  R25 = Resistor [tolerance=±5% resistance=10k power=0.25 package="0603 [SMD]"]
  R23 = Resistor [tolerance=±5% resistance=10k power=0.25 package="0603 [SMD]"]
  C7 = Ceramic Capacitor [capacitance="100 nF" voltage=35V package="0603 [SMD, multilayer]"]
  C8 = Ceramic Capacitor [capacitance="100 nF" voltage=35V package="0603 [SMD, multilayer]"]
  R19 = Resistor [tolerance=±5% resistance=10k power=0.25 package="0603 [SMD]"]
  R12 = Resistor [tolerance=±5% resistance=10k power=0.25 package="0603 [SMD]"]
  R13 = Resistor [tolerance=±5% resistance=1k power=0.25 package="0603 [SMD]"]
  R14 = Resistor [tolerance=±5% resistance=1k power=0.25 package="0603 [SMD]"]
  R21 = Resistor [tolerance=±5% resistance=10k power=0.25 package="0603 [SMD]"]
  R18 = Resistor [tolerance=±5% resistance=10k power=0.25 package="0603 [SMD]"]
  U7 = 74AHC1G08 [package=sot23-5]
  C3 = Ceramic Capacitor [capacitance="100 nF" voltage=35V package="0603 [SMD, multilayer]"]
  J16 = male pin header, 2 pins [form="♂ (male)"]
  J17 = male pin header, 2 pins [form="♂ (male)"]
  J14 = male pin header, 2 pins [form="♂ (male)"]
  J15 = male pin header, 2 pins [form="♂ (male)"]
  C14 = Ceramic Capacitor [capacitance=1µF voltage=35V package="0805 [SMD, multilayer]"]
  U1 = Voltage Regulator - Variable [package="TO220 [THT]"]
  C4 = Ceramic Capacitor [capacitance=10µF voltage=35V package="0805 [SMD, multilayer]"]
  R11 = Resistor [tolerance=±5% resistance=10k power=0.25 package="0603 [SMD]"]
  C9 = Ceramic Capacitor [capacitance="100 nF" voltage=35V package="0603 [SMD, multilayer]"]
  C10 = Ceramic Capacitor [capacitance="100 nF" voltage=35V package="0603 [SMD, multilayer]"]
  C11 = Ceramic Capacitor [capacitance="100 nF" voltage=35V package="0603 [SMD, multilayer]"]
  C12 = Ceramic Capacitor [capacitance="100 nF" voltage=35V package="0603 [SMD, multilayer]"]
  U11 = SN74LVC1G18DBVR [package=sot-23-6]
  U10 = SN74LVC1G18DBVR [package=sot-23-6]
  U9 = SN74LVC1G18DBVR [package=sot-23-6]
  U8 = SN74LVC1G18DBVR [package=sot-23-6]
  U5 = CD4051BE 8-channel mux [chip_label=IC package="DIP (Dual Inline) [THT]"]
  J13 = male pin header, 2 pins [form="♂ (male)"]
  U4 = MX1508 Motor Driver [chip_label=SOIC18-W package=SO]
  C2 = Capacitor Polarized [package=panasonic_d]
  R4 = Resistor [tolerance=±5% resistance=220 package="0805 [SMD]"]
  C1 = Capacitor Polarized [package=panasonic_d]
  U6 = Voltage Regulator - Variable [package="TO220 [THT]"]
  R16 = Resistor [tolerance=±5% resistance=10k power=0.25 package="0603 [SMD]"]
  C13 = Ceramic Capacitor [capacitance=10µF voltage=35V package="0805 [SMD, multilayer]"]
  R17 = Resistor [tolerance=±5% resistance=10k power=0.25 package="0603 [SMD]"]
  D16 = Diode [package=sma-diode-kit]
  J34 = male pin header, 2 pins [form="♂ (male)"]
  J35 = male pin header, 3 pins [form="♂ (male)"]
  J36 = male pin header, 5 pins [form="♂ (male)"]
  J37 = male pin header, 4 pins [form="♂ (male)"]
  R20 = Resistor [tolerance=±5% resistance=10k power=0.25 package="0603 [SMD]"]
  C15 = Ceramic Capacitor [capacitance="100 nF" voltage=35V package="0603 [SMD, multilayer]"]
  C16 = Ceramic Capacitor [capacitance="100 nF" voltage=35V package="0603 [SMD, multilayer]"]
  C17 = Ceramic Capacitor [capacitance="100 nF" voltage=35V package="0603 [SMD, multilayer]"]
  C18 = Ceramic Capacitor [capacitance="100 nF" voltage=35V package="0603 [SMD, multilayer]"]
  C19 = Ceramic Capacitor [capacitance="100 nF" voltage=35V package="0603 [SMD, multilayer]"]
  D21 = Diode [package=sma-diode]
  C20 = Ceramic Capacitor [capacitance="100 nF" voltage=35V package="0603 [SMD, multilayer]"]
  C21 = Ceramic Capacitor [capacitance="100 nF" voltage=35V package="0603 [SMD, multilayer]"]
  C23 = Ceramic Capacitor [capacitance="100 nF" voltage=35V package="0603 [SMD, multilayer]"]
  C22 = Ceramic Capacitor [capacitance=47nF voltage=35V package="0603 [SMD, multilayer]"]
  C24 = Ceramic Capacitor [capacitance=47nF voltage=35V package="0603 [SMD, multilayer]"]
  U22 = MC74VHC1G32DTT1G [package=sot23-5]
  U19 = MC74VHC1G32DTT1G [package=sot23-5]
  U23 = MC74VHC1G32DTT1G [package=sot23-5]
  U21 = MC74VHC1G32DTT1G [package=sot23-5]
  U20 = MC74VHC1G32DTT1G [package=sot23-5]
  U18 = MC74VHC1G32DTT1G [package=sot23-5]
  C6 = Ceramic Capacitor [capacitance="100 nF" voltage=35V package="0603 [SMD, multilayer]"]
  U24 = 74AHC1G08 [package=sot23-5]
  C25 = Ceramic Capacitor [capacitance="100 nF" voltage=35V package="0603 [SMD, multilayer]"]
  J38 = male pin header, 2 pins [form="♂ (male)"]
  R26 = Resistor [tolerance=±5% resistance=1k power=0.25 package="0603 [SMD]"]
  J39 = male pin header, 2 pins [form="♂ (male)"]
  J40 = male pin header, 1 pin [form="♂ (male)"]

nets:
  GND: A1.GND, U3.0V, U2.0V, J24.pin3, J25.pin3, J19.pin4, J1.pin2, R24.Pin_1, R22.Pin_1, R25.Pin_1, R23.Pin_1, C7.0, C8.1, R19.Pin_0, R12.Pin_1, R13.Pin_1, R14.Pin_1, R21.Pin_0, R18.Pin_0, U7.GND, C3.1, C14.1, U1.GND, C4.1, R11.Pin_1, C9.0, C10.0, C11.1, C12.1, U11.GND, U10.GND, U9.GND, U8.GND, U5.Negative, U5.Ground, U4.idk_(connect_to_ground), C2.-, C1.-, U6.GND, R16.Pin_1, C13.1, R17.Pin_0, D16.A, J35.pin3, J36.pin4, J37.pin4, R20.Pin_0, C15.0, C16.0, C17.0, C18.1, C19.1, C20.1, C21.0, C23.0, C22.0, C24.0, U22.GND, U19.GND, U23.GND, U21.GND, U20.GND, U18.GND, C6.1, U24.GND, C25.1, R26.Pin_1
  N1: A1.D2, U11.S, U10.S, U9.S, U8.S
  N2: A1.D3, U8.A
  N3: A1.D4, U9.A
  N4: A1.D5, U10.A
  N5: A1.D6, U11.A
  N6: A1.D7, U5.Selector_C
  N7: A1.D8, U5.Selector_B
  N8: A1.D9, U5.Selector_A
  N9: A1.D10, U5.COM_I/O
  N10: A1.D11/MOSI, U4.Motor_1_logic_1
  N11: A1.D12/MISO, U4.Motor_1_logic_2
  VCC: A1.VIN, J3.pin5, J4.pin2, J4.pin5, J28.pin1, J24.pin2, J25.pin2, J19.pin15, U7.VCC, C3.0, J16.pin1, J17.pin1, J14.pin1, J15.pin1, C14.0, U1.OUT, C4.0, R11.Pin_0, C9.1, C10.1, C11.0, C12.0, U11.VDD, U10.VDD, U9.VDD, U8.VDD, U5.5v_input, J34.pin2, J35.pin2, J37.pin2, C15.1, C16.1, C17.1, C18.0, C19.0, C20.0, U22.VCC, U19.VCC, U23.VCC, U21.VCC, U20.VCC, U18.VCC, C6.0, U24.VCC, C25.0, J38.pin1, J39.pin1
  N12: A1.A7, J28.pin3, J19.pin13, U18.B
  N13: A1.A6, J28.pin4, J19.pin14, U18.A
  N14: A1.A5, J37.pin3
  N15: A1.A4, J37.pin1
  N16: A1.A3, J25.pin1
  N17: A1.A2, J24.pin1, J19.pin16, U7.A
  N18: A1.A1, J28.pin2, J19.pin3, J39.pin2
  N19: A1.A0, J40.pin1
  N20: A1.D13/SCK, U24.B
  N21: J3.pin1, J3.pin3, U1.IN, U6.IN, J36.pin5
  N22: J3.pin2, D21.C
  N23: J3.pin6, J19.pin6, R19.Pin_1, U5.Ch_7
  N24: J4.pin1, J4.pin3, J19.pin5, U21.B
  N25: J4.pin6, U20.A
  N26: J28.pin5, R12.Pin_0
  N27: J28.pin6, R13.Pin_0
  N28: J28.pin7, R26.Pin_0
  N29: J28.pin8, R14.Pin_0
  N30: U3.In_1, U11.Y1
  N31: U3.In_2, U10.Y1
  N32: U3.In_3, U9.Y1
  N33: U3.In_4, U8.Y1
  N34: U3.COM_-_Common, U2.COM_-_Common, J10.pin1, J11.pin1, C7.1, C8.0, U4.+5v_(VDD2_-_use_this_one), C2.+, R4.Pin_0, U6.OUT, R16.Pin_0, C13.0, C21.1, C23.1, C22.1, C24.1
  N35: U3.Out_4, J11.pin5
  N36: U3.Out_3, J11.pin4
  N37: U3.Out_2, J11.pin3
  N38: U3.Out_1, J11.pin2
  N39: U2.In_1, U11.Y0
  N40: U2.In_2, U10.Y0
  N41: U2.In_3, U9.Y0
  N42: U2.In_4, U8.Y0
  N43: U2.Out_4, J10.pin5
  N44: U2.Out_3, J10.pin4
  N45: U2.Out_2, J10.pin3
  N46: U2.Out_1, J10.pin2
  N47: J19.pin7, U22.B
  N48: J19.pin8, U23.B
  N49: J19.pin9, U21.A
  N50: J19.pin10, U19.A
  N51: J19.pin11, J34.pin1, U19.B
  N52: J19.pin12, U20.B
  N53: J1.pin1, D21.A
  N54: R24.Pin_0, U5.Ch_1, U22.Y
  N55: R22.Pin_0, U5.Ch_3, J36.pin2, U19.Y
  N56: R25.Pin_0, U5.Ch_2, U23.Y
  N57: R23.Pin_0, U5.Ch_0, J36.pin1, U20.Y
  N58: R21.Pin_1, U5.Ch_4, J38.pin2
  N59: R18.Pin_1, J14.pin2, U5.Ch_5
  N60: U7.B, U24.Y
  N61: U7.Y, J36.pin3
  N62: J16.pin2, U22.A
  N63: J17.pin2, U23.A
  N64: J15.pin2, U5.Ch_6, R20.Pin_1
  N65: U5.Disable_channels, R17.Pin_1
  N66: J13.pin1, U4.Motor_1_out_2
  N67: J13.pin2, U4.Motor_1_out_1
  N68: U4.VCC1, U4.VCC2, R4.Pin_1, C1.+, D16.C
  N69: J35.pin1, U18.Y
  N70: U21.Y, U24.A

notes:
  Power SW
  Speed SW
  LEDs
  PW SW
  Vertical Motor
  Horiz. Motor
  [
  Upper Limit
  Lower Limit
  V MTR
  H MTR
  Pause Button
  Play/Home Button
  U LIM
  L LIM
  PA BT
  PL BT
  Home Sensor
  HOME
  Pickup Encoder
  Speed Sensor
  SPD.
  ENC.
  SPD SW
  Automatic Changer Comm
  GND
  +5v
  5v DC
  3.3v DC
  Mux S16
  Mux S15
  Auto-mode indicator (Mux S12)
  5v DC in
  5v DC out
  NC
  Turntable power indicator LED
  33-RPM pot
  J12 pin 2
  45-RPM pot
  J12 pin 3
  J12 pin 4
  Q3 drain
  J10 pin 5
  Power indicator LED (5v)
  Turntable power indicator LED (J10 pin 3)
  Pause status LED (Ard. D13)
  Play status LED (Ard. D12)
  Play status LED GND
  Pause status LED GND
  Turntable power indicator LED GND
  Power indicator LED GND
  SW 1
  SW 2
  SW 3
  SW 4
  SW 5
  SW 6
  _
  Automatic Record Player v0.5 (Dec. 2022)
  Patrick N. (github.com/pdnelson)
  12v DC in
  12v DC
  -
  +
  Main 5v circuit
  ]
  Horizontal Engagement Motor Controller
  Horizontal Engagement Motor
  CLTC
  Alt. Speed Button
  SPD 2
  AUD.
  TRN MTR
  Turn Motor Comm
  Motor 5v Circuit
  Wait Until Target Speed
  WAIT
  Repeat
  RPT
  Lift Indicator
  LIFT

custom parts:
  Voltage Regulator - Variable: Variable DC Voltage Regulator
  CD4051BE 8-channel mux: A DIP stand-in part for whatever IC you want. With 16 pins on a 300mil dual inline package (DIP) footprint.
  MC74VHC1G32DTT1G: Single 2-input OR gate
